// Logisim project assignment3-1.2.circ as structural Verilog
module main (
  input  in_1,
  input  in_2,
  input  D,
  input  EN,
  input  in_5,
  input  in_6,
  input  in_7,
  input  in_8,
  output out_9,
  output out_10,
  output Q,
  output QN,
  output out_13,
  output out_14,
  output out_15
);

  wire dlatch_1_q, nand_1_out, nand_2_out, nand_3_out, nand_4_out, nand_7_out, nand_8_out, nand_9_out,
       nand_10_out, not_1_out, not_2_out, not_3_out, not_4_out, not_5_out, not_6_out;

  not not_1 (not_1_out, in_6);
  not not_2 (not_2_out, D);
  not not_3 (not_3_out, in_8);
  nand nand_1 (nand_1_out, D, EN);
  nand nand_2 (nand_2_out, EN, not_2_out);
  not not_4 (not_4_out, in_7);
  d_latch d_latch_1 (.en(in_1), .d(in_2), .q(out_9), .qn(out_10));
  dlatch dlatch_1 (.D(in_5), .EN(not_1_out), .Q(dlatch_1_q));  // open: QN
  nand nand_3 (nand_3_out, in_7, not_3_out);
  nand nand_4 (nand_4_out, not_3_out, not_4_out);
  nand nand_5 (Q, nand_1_out, QN);
  nand nand_6 (QN, Q, nand_2_out);
  nand nand_7 (nand_7_out, nand_3_out, nand_8_out);
  nand nand_8 (nand_8_out, nand_7_out, nand_4_out);
  not not_5 (not_5_out, not_3_out);
  not not_6 (not_6_out, nand_7_out);
  dlatch dlatch_2 (.D(dlatch_1_q), .EN(in_6), .Q(out_13));  // open: QN
  nand nand_9 (nand_9_out, nand_7_out, not_5_out);
  nand nand_10 (nand_10_out, not_5_out, not_6_out);
  nand nand_11 (out_14, nand_9_out, out_15);
  nand nand_12 (out_15, out_14, nand_10_out);
endmodule

module dlatch (
  input  D,
  input  EN,
  output Q,
  output QN
);

  wire nand_1_out, nand_2_out, not_1_out;

  not not_1 (not_1_out, D);
  nand nand_1 (nand_1_out, D, EN);
  nand nand_2 (nand_2_out, EN, not_1_out);
  nand nand_3 (Q, nand_1_out, QN);
  nand nand_4 (QN, Q, nand_2_out);
endmodule

module dff_ms (
  input  D,
  input  CLK,
  input  in_3,
  input  in_4,
  output Q,
  output NQ,
  output out_7
);

  wire nand_1_out, nand_2_out, nand_3_out, nand_4_out, nand_5_out, nand_6_out, not_1_out, not_2_out,
       not_3_out, not_4_out;

  not not_1 (not_1_out, CLK);
  not not_2 (not_2_out, D);
  nand nand_1 (nand_1_out, D, not_1_out);
  nand nand_2 (nand_2_out, not_1_out, not_2_out);
  nand nand_3 (nand_3_out, nand_1_out, nand_4_out);
  nand nand_4 (nand_4_out, nand_3_out, nand_2_out);
  not not_3 (not_3_out, not_1_out);
  d_ff d_ff_1 (.clk(in_3), .d(in_4), .q(out_7));
  not not_4 (not_4_out, nand_3_out);
  nand nand_5 (nand_5_out, nand_3_out, not_3_out);
  nand nand_6 (nand_6_out, not_3_out, not_4_out);
  nand nand_7 (Q, nand_5_out, NQ);
  nand nand_8 (NQ, Q, nand_6_out);
endmodule

// VHDL entity rs_latch, as the project stores it:
library ieee;
use ieee.std_logic_1164.all;

entity rs_latch is
    port (
        r, s : in  std_logic;
        q    : out std_logic;
        qn   : out std_logic
    );
end entity rs_latch;

architecture bhv of rs_latch is
    signal q_i  : std_logic := '0';
    signal qn_i : std_logic := '1';
begin
    process(s, r)
    begin
        if s = '1' and r = '1' then      -- forbidden: both outputs 0
            q_i <= '0'; qn_i <= '0';
        elsif s = '1' then               -- set
            q_i <= '1'; qn_i <= '0';
        elsif r = '1' then               -- reset
            q_i <= '0'; qn_i <= '1';
        end if;                          -- s=0, r=0: hold
    end process;
    q  <= q_i;
    qn <= qn_i;
end architecture bhv;

// VHDL entity d_latch, as the project stores it:
library ieee;
use ieee.std_logic_1164.all;

entity d_latch is
    port (
        en : in  std_logic;
        d  : in  std_logic;
        q  : out std_logic;
        qn : out std_logic
    );
end entity d_latch;

architecture bhv of d_latch is
    signal q_i : std_logic := '0';
begin
    process(en, d)
    begin
        if en = '1' then
            q_i <= d;
        end if;                          -- en=0: hold
    end process;
    q  <= q_i;
    qn <= not q_i;
end architecture bhv;

// VHDL entity d_ff, as the project stores it:
library ieee;
use ieee.std_logic_1164.all;

entity d_ff is
    port (
        clk : in  std_logic;
        d   : in  std_logic;
        q   : out std_logic
    );
end entity d_ff;

architecture bhv of d_ff is
    signal q_i : std_logic := '0';
begin
    process(clk)
    begin
        if rising_edge(clk) then
            q_i <= d;
        end if;
    end process;
    q <= q_i;
end architecture bhv;
