// Logisim project assignment3-3.4.5.circ as structural Verilog
module main (
  input  in_1,
  input  in_2,
  input  in_3,
  input  in_4,
  input  in_5,
  input  J,
  input  CLK,
  input  in_8,
  input  K,
  input  in_10,
  input  in_11,
  input  in_12,
  input  in_13,
  output out_14,
  output out_15,
  output Q,
  output NQ,
  output out_18
);

  wire nand_1_out, nand_2_out;

  nand nand_1 (nand_1_out, NQ, J, CLK);
  nand nand_2 (nand_2_out, CLK, K, Q);
  d_ff d_ff_1 (.clk(in_1), .d(in_2), .q(out_14));
  jk_ff jk_ff_1 (.clk(in_3), .j(in_4), .k(in_5), .q(out_15));
  nand nand_3 (Q, nand_1_out, NQ);
  nand nand_4 (NQ, Q, in_8, nand_2_out);
  d_ff_sc d_ff_sc_1 (.clk(in_10), .d(in_11), .clr(in_12), .set(in_13), .q(out_18));
endmodule

module jkff (
  input  J,
  input  CLK,
  input  in_3,
  input  K,
  output Q,
  output NQ
);

  wire nand_1_out, nand_2_out;

  nand nand_1 (nand_1_out, NQ, J, CLK);
  nand nand_2 (nand_2_out, CLK, K, Q);
  nand nand_3 (Q, nand_1_out, NQ);
  nand nand_4 (NQ, Q, in_3, nand_2_out);
endmodule

// VHDL entity d_ff, as the project stores it:
library ieee;
use ieee.std_logic_1164.all;

entity d_ff is
    port (
        clk : in  std_logic;
        d   : in  std_logic;
        q   : out std_logic
    );
end entity d_ff;

architecture bhv of d_ff is
    signal q_i : std_logic := '0';
begin
    process(clk)
    begin
        if rising_edge(clk) then
            q_i <= d;
        end if;
    end process;
    q <= q_i;
end architecture bhv;

// VHDL entity jk_ff, as the project stores it:
library ieee;
use ieee.std_logic_1164.all;

entity jk_ff is
    port (
        clk : in  std_logic;
        j   : in  std_logic;
        k   : in  std_logic;
        q   : out std_logic
    );
end entity jk_ff;

architecture bhv of jk_ff is
    signal q_i : std_logic := '0';
begin
    process(clk)
    begin
        if rising_edge(clk) then
            if    j = '0' and k = '0' then q_i <= q_i;      -- hold
            elsif j = '0' and k = '1' then q_i <= '0';      -- reset
            elsif j = '1' and k = '0' then q_i <= '1';      -- set
            else                           q_i <= not q_i;  -- toggle
            end if;
        end if;
    end process;
    q <= q_i;
end architecture bhv;

// VHDL entity d_ff_sc, as the project stores it:
library ieee;
use ieee.std_logic_1164.all;

entity d_ff_sc is
    port (
        clk : in  std_logic;
        d   : in  std_logic;
        clr : in  std_logic;   -- asynchronous clear (highest priority)
        set : in  std_logic;   -- asynchronous set
        q   : out std_logic
    );
end entity d_ff_sc;

architecture bhv of d_ff_sc is
begin
    process(clk, clr, set)
    begin
        if clr = '1' then
            q <= '0';
        elsif set = '1' then
            q <= '1';
        elsif rising_edge(clk) then
            q <= d;
        end if;
    end process;
end architecture bhv;
